# Fritzing sketch Diagrama de conexion (saved by Fritzing 0.9.3b)
breadboards: 1

parts:
  Part1 = Arduino Uno (Rev3)
  U1 = WS2812 RGB LED strip
  U2 = LIPO-1000mAh [package=lipo-1000]
  C1 = Capacitor Polarized [package=cpol-radial-1000uf-25v]

nets:
  N1: Part1.D8, U1.DIN
  GND: Part1.GND, U1.GND, U2.-, C1.-
  N2: U1.VCC, U2.+, C1.+

custom parts:
  WS2812 RGB LED strip: WS2812 strip
  LIPO-1000mAh: 1000mAh Lipo-battery
